// Logisim project CPU.circ as structural Verilog: 20 circuits, main circuit main
module main (
  input  Jump,
  input  Branch,
  input  [2:0] ALUOp
);

  wire and_1_out, clock_1_out, controlunit_1_alusrc, controlunit_1_b_prime_cin, controlunit_1_l_r,
       controlunit_1_load, controlunit_1_memread, controlunit_1_regdst, controlunit_1_regwrite,
       controlunit_1_shift, controlunit_1_store, n16_bit_alu_1_f;
  wire [3:0] multiplexer_1_out, rom_1_data;
  wire [7:0] adder_1_out, adder_2_out, bit_extender_2_out, bit_extender_3_out, multiplexer_3_out,
       multiplexer_4_out, PC_q;
  wire [11:0] rom_1_data_2;
  wire [15:0] bit_extender_1_out, multiplexer_2_out, multiplexer_5_out, multiplexer_6_out,
       n16_bit_alu_1_out_7, n16bit_sll_srl_1_out_4, ram_1_data, register_file_1_register_1_data,
       register_file_1_register_2_data;

  ControlUnit controlunit_1 (
    .Opcode(rom_1_data), .RegWrite(controlunit_1_regwrite), .Regdst(controlunit_1_regdst),
    .AluSrc(controlunit_1_alusrc), .MemRead(controlunit_1_memread), .ALUop(ALUOp), .Branch(Branch),
    .Jump(Jump), .Load(controlunit_1_load), .Store(controlunit_1_store),
    .B_prime_Cin(controlunit_1_b_prime_cin), .L_R(controlunit_1_l_r), .Shift(controlunit_1_shift));
  Register PC (.D(multiplexer_4_out), .Q(PC_q), .clk(clock_1_out));  // open: en, clr
  Clock clock_1 (.out(clock_1_out));
  Adder adder_1 (.a(PC_q), .b(8'h1), .out(adder_1_out));  // open: cin, cout
  ROM #(.dataWidth(16)) rom_1 (.addr(PC_q), .data({rom_1_data, rom_1_data_2}));  // open: sel
  Multiplexer #(.width(4)) multiplexer_1 (
    .in0(rom_1_data_2[3:0]), .in1(rom_1_data_2[7:4]), .out(multiplexer_1_out), .sel(controlunit_1_regdst));  // open: en
  assign bit_extender_1_out = {{12{rom_1_data_2[3]}}, rom_1_data_2[3:0]};  // Bit_Extender bit_extender_1
  Bit_Extender #(.in_width(12), .out_width(8)) bit_extender_2 (.in(rom_1_data_2), .out(bit_extender_2_out));
  Register_file register_file_1 (
    .Data(multiplexer_6_out), .CLK(clock_1_out), .Register_1_Data(register_file_1_register_1_data),
    .Register_2_Data(register_file_1_register_2_data), .Write_Register(multiplexer_1_out),
    .Write_register_2(controlunit_1_regwrite), .Read_Register_1(rom_1_data_2[11:8]),
    .Read_Register_2(rom_1_data_2[7:4]));
  Adder adder_2 (.a(adder_1_out), .b(bit_extender_3_out), .out(adder_2_out));  // open: cin, cout
  Bit_Extender #(.in_width(16), .out_width(8)) bit_extender_3 (.in(bit_extender_1_out), .out(bit_extender_3_out));
  Multiplexer #(.width(16)) multiplexer_2 (
    .in0(register_file_1_register_2_data), .in1(bit_extender_1_out), .out(multiplexer_2_out),
    .sel(controlunit_1_alusrc));  // open: en
  _16_bit_ALU u_16_bit_alu_1 (
    .in_1(register_file_1_register_1_data), .B(multiplexer_2_out), .Cin(controlunit_1_b_prime_cin),
    .F(n16_bit_alu_1_f), .out_7(n16_bit_alu_1_out_7), .B_prime(controlunit_1_b_prime_cin), .OP(ALUOp));  // open: Cout
  and and_1 (and_1_out, Branch, n16_bit_alu_1_f);
  _16bit_sll_srl u_16bit_sll_srl_1 (
    .in_1(register_file_1_register_1_data), .in_2(rom_1_data_2[3:0]), .in_3(controlunit_1_l_r),
    .out_4(n16bit_sll_srl_1_out_4));
  Multiplexer #(.width(8)) multiplexer_3 (
    .in0(adder_1_out), .in1(adder_2_out), .out(multiplexer_3_out), .sel(and_1_out));  // open: en
  Multiplexer #(.width(8)) multiplexer_4 (
    .in0(multiplexer_3_out), .in1(bit_extender_2_out), .out(multiplexer_4_out), .sel(Jump));  // open: en
  RAM #(.addrWidth(16), .dataWidth(16), .bus("separate")) ram_1 (
    .addr(n16_bit_alu_1_out_7), .din(register_file_1_register_2_data), .data(ram_1_data),
    .str(controlunit_1_store), .clk(clock_1_out), .ld(controlunit_1_load));  // open: sel, clr
  Multiplexer #(.width(16)) multiplexer_5 (
    .in0(n16_bit_alu_1_out_7), .in1(ram_1_data), .out(multiplexer_5_out), .sel(controlunit_1_memread));  // open: en
  Multiplexer #(.width(16)) multiplexer_6 (
    .in0(multiplexer_5_out), .in1(n16bit_sll_srl_1_out_4), .out(multiplexer_6_out), .sel(controlunit_1_shift));  // open: en

  // Notes on the sheet:
  //   contents of rom_1 (hex, n*v repeats v):
  //   8*0 5393 6652 e236 7131 176 f004
endmodule

module Register_file (
  input  [3:0] Read_Register_1,
  input  [3:0] Write_Register,
  input  Write_register_2,
  input  [15:0] Data,
  input  CLK,
  input  [3:0] Read_Register_2,
  output [15:0] Register_1_Data,
  output [15:0] Register_2_Data
);

  wire decoder_1_out0, decoder_1_out1, decoder_1_out2, decoder_1_out3, decoder_1_out4, decoder_1_out5,
       decoder_1_out6, decoder_1_out7, decoder_1_out8, decoder_1_out9, decoder_1_out10, decoder_1_out11,
       decoder_1_out12, decoder_1_out13, decoder_1_out14, decoder_1_out15;
  wire [15:0] a0_q, fp_q, gp_q, multiplexer_1_out, ra_q, s0_q, s1_q, s2_q, s3_q, s4_q, s5_q, sp_q, t1_q,
       t2_q, t3_q, to_q, zero_q;

  Decoder #(.select(4)) decoder_1 (
    .out0(decoder_1_out0), .out1(decoder_1_out1), .out2(decoder_1_out2), .out3(decoder_1_out3),
    .out4(decoder_1_out4), .out5(decoder_1_out5), .out6(decoder_1_out6), .out7(decoder_1_out7),
    .out8(decoder_1_out8), .out9(decoder_1_out9), .out10(decoder_1_out10), .out11(decoder_1_out11),
    .out12(decoder_1_out12), .out13(decoder_1_out13), .out14(decoder_1_out14), .out15(decoder_1_out15),
    .sel(Write_Register));  // open: en
  Multiplexer #(.width(16)) multiplexer_1 (
    .in1(Data), .out(multiplexer_1_out), .sel(Write_register_2));  // open: in0, en
  Register #(.width(16)) zero (.D(multiplexer_1_out), .en(decoder_1_out0), .Q(zero_q), .clk(CLK));  // open: clr
  Register #(.width(16)) to (.D(multiplexer_1_out), .en(decoder_1_out1), .Q(to_q), .clk(CLK));  // open: clr
  Register #(.width(16)) t1 (.D(multiplexer_1_out), .en(decoder_1_out2), .Q(t1_q), .clk(CLK));  // open: clr
  Register #(.width(16)) t2 (.D(multiplexer_1_out), .en(decoder_1_out3), .Q(t2_q), .clk(CLK));  // open: clr
  Register #(.width(16)) t3 (.D(multiplexer_1_out), .en(decoder_1_out4), .Q(t3_q), .clk(CLK));  // open: clr
  Register #(.width(16)) s0 (.D(multiplexer_1_out), .en(decoder_1_out5), .Q(s0_q), .clk(CLK));  // open: clr
  Register #(.width(16)) s1 (.D(multiplexer_1_out), .en(decoder_1_out6), .Q(s1_q), .clk(CLK));  // open: clr
  Register #(.width(16)) s2 (.D(multiplexer_1_out), .en(decoder_1_out7), .Q(s2_q), .clk(CLK));  // open: clr
  Register #(.width(16)) s3 (.D(multiplexer_1_out), .en(decoder_1_out8), .Q(s3_q), .clk(CLK));  // open: clr
  Register #(.width(16)) s4 (.D(multiplexer_1_out), .en(decoder_1_out9), .Q(s4_q), .clk(CLK));  // open: clr
  Register #(.width(16)) s5 (.D(multiplexer_1_out), .en(decoder_1_out10), .Q(s5_q), .clk(CLK));  // open: clr
  Register #(.width(16)) gp (.D(multiplexer_1_out), .en(decoder_1_out11), .Q(gp_q), .clk(CLK));  // open: clr
  Register #(.width(16)) sp (.D(multiplexer_1_out), .en(decoder_1_out12), .Q(sp_q), .clk(CLK));  // open: clr
  Register #(.width(16)) fp (.D(multiplexer_1_out), .en(decoder_1_out13), .Q(fp_q), .clk(CLK));  // open: clr
  Register #(.width(16)) ra (.D(multiplexer_1_out), .en(decoder_1_out14), .Q(ra_q), .clk(CLK));  // open: clr
  Register #(.width(16)) a0 (.D(multiplexer_1_out), .en(decoder_1_out15), .Q(a0_q), .clk(CLK));  // open: clr
  Multiplexer #(.select(4), .width(16)) multiplexer_2 (
    .in0(zero_q), .in1(to_q), .in2(t1_q), .in3(t2_q), .in4(t3_q), .in5(s0_q), .in6(s1_q), .in7(s2_q),
    .in8(s3_q), .in9(s4_q), .in10(s5_q), .in11(gp_q), .in12(sp_q), .in13(fp_q), .in14(ra_q), .in15(a0_q),
    .out(Register_1_Data), .sel(Read_Register_1));  // open: en
  Multiplexer #(.select(4), .width(16)) multiplexer_3 (
    .in0(zero_q), .in1(to_q), .in2(t1_q), .in3(t2_q), .in4(t3_q), .in5(s0_q), .in6(s1_q), .in7(s2_q),
    .in8(s3_q), .in9(s4_q), .in10(s5_q), .in11(gp_q), .in12(sp_q), .in13(fp_q), .in14(ra_q), .in15(a0_q),
    .out(Register_2_Data), .sel(Read_Register_2));  // open: en
endmodule

module _16bit_SLL (
  input  [15:0] in_1,
  input  [3:0] SRL,
  output [15:0] out_3
);

  Multiplexer #(.select(4)) multiplexer_1 (
    .in0(in_1[0]), .in1(1'b0), .in2(1'b0), .in3(1'b0), .in4(1'b0), .in5(1'b0), .in6(1'b0), .in7(1'b0),
    .in8(1'b0), .in9(1'b0), .in10(1'b0), .in11(1'b0), .in12(1'b0), .in13(1'b0), .in14(1'b0), .in15(1'b0),
    .out(out_3[0]), .sel(SRL));  // open: en
  Multiplexer #(.select(4)) multiplexer_2 (
    .in0(in_1[1]), .in1(in_1[0]), .in2(1'b0), .in3(1'b0), .in4(1'b0), .in5(1'b0), .in6(1'b0), .in7(1'b0),
    .in8(1'b0), .in9(1'b0), .in10(1'b0), .in11(1'b0), .in12(1'b0), .in13(1'b0), .in14(1'b0), .in15(1'b0),
    .out(out_3[1]), .sel(SRL));  // open: en
  Multiplexer #(.select(4)) multiplexer_3 (
    .in0(in_1[2]), .in1(in_1[1]), .in2(in_1[0]), .in3(1'b0), .in4(1'b0), .in5(1'b0), .in6(1'b0), .in7(1'b0),
    .in8(1'b0), .in9(1'b0), .in10(1'b0), .in11(1'b0), .in12(1'b0), .in13(1'b0), .in14(1'b0), .in15(1'b0),
    .out(out_3[2]), .sel(SRL));  // open: en
  Multiplexer #(.select(4)) multiplexer_4 (
    .in0(in_1[3]), .in1(in_1[2]), .in2(in_1[1]), .in3(in_1[0]), .in4(1'b0), .in5(1'b0), .in6(1'b0),
    .in7(1'b0), .in8(1'b0), .in9(1'b0), .in10(1'b0), .in11(1'b0), .in12(1'b0), .in13(1'b0), .in14(1'b0),
    .in15(1'b0), .out(out_3[3]), .sel(SRL));  // open: en
  Multiplexer #(.select(4)) multiplexer_5 (
    .in0(in_1[4]), .in1(in_1[3]), .in2(in_1[2]), .in3(in_1[1]), .in4(in_1[0]), .in5(1'b0), .in6(1'b0),
    .in7(1'b0), .in8(1'b0), .in9(1'b0), .in10(1'b0), .in11(1'b0), .in12(1'b0), .in13(1'b0), .in14(1'b0),
    .in15(1'b0), .out(out_3[4]), .sel(SRL));  // open: en
  Multiplexer #(.select(4)) multiplexer_6 (
    .in0(in_1[5]), .in1(in_1[4]), .in2(in_1[3]), .in3(in_1[2]), .in4(in_1[1]), .in5(in_1[0]), .in6(1'b0),
    .in7(1'b0), .in8(1'b0), .in9(1'b0), .in10(1'b0), .in11(1'b0), .in12(1'b0), .in13(1'b0), .in14(1'b0),
    .in15(1'b0), .out(out_3[5]), .sel(SRL));  // open: en
  Multiplexer #(.select(4)) multiplexer_7 (
    .in0(in_1[6]), .in1(in_1[5]), .in2(in_1[4]), .in3(in_1[3]), .in4(in_1[2]), .in5(in_1[1]), .in6(in_1[0]),
    .in7(1'b0), .in8(1'b0), .in9(1'b0), .in10(1'b0), .in11(1'b0), .in12(1'b0), .in13(1'b0), .in14(1'b0),
    .in15(1'b0), .out(out_3[6]), .sel(SRL));  // open: en
  Multiplexer #(.select(4)) multiplexer_8 (
    .in0(in_1[7]), .in1(in_1[6]), .in2(in_1[5]), .in3(in_1[4]), .in4(in_1[3]), .in5(in_1[2]), .in6(in_1[1]),
    .in7(in_1[0]), .in8(1'b0), .in9(1'b0), .in10(1'b0), .in11(1'b0), .in12(1'b0), .in13(1'b0), .in14(1'b0),
    .in15(1'b0), .out(out_3[7]), .sel(SRL));  // open: en
  Multiplexer #(.select(4)) multiplexer_9 (
    .in0(in_1[8]), .in1(in_1[7]), .in2(in_1[6]), .in3(in_1[5]), .in4(in_1[4]), .in5(in_1[3]), .in6(in_1[2]),
    .in7(in_1[1]), .in8(in_1[0]), .in9(1'b0), .in10(1'b0), .in11(1'b0), .in12(1'b0), .in13(1'b0),
    .in14(1'b0), .in15(1'b0), .out(out_3[8]), .sel(SRL));  // open: en
  Multiplexer #(.select(4)) multiplexer_10 (
    .in0(in_1[9]), .in1(in_1[8]), .in2(in_1[7]), .in3(in_1[6]), .in4(in_1[5]), .in5(in_1[4]), .in6(in_1[3]),
    .in7(in_1[2]), .in8(in_1[1]), .in9(in_1[0]), .in10(1'b0), .in11(1'b0), .in12(1'b0), .in13(1'b0),
    .in14(1'b0), .in15(1'b0), .out(out_3[9]), .sel(SRL));  // open: en
  Multiplexer #(.select(4)) multiplexer_11 (
    .in0(in_1[10]), .in1(in_1[9]), .in2(in_1[8]), .in3(in_1[7]), .in4(in_1[6]), .in5(in_1[5]), .in6(in_1[4]),
    .in7(in_1[3]), .in8(in_1[2]), .in9(in_1[1]), .in10(in_1[0]), .in11(1'b0), .in12(1'b0), .in13(1'b0),
    .in14(1'b0), .in15(1'b0), .out(out_3[10]), .sel(SRL));  // open: en
  Multiplexer #(.select(4)) multiplexer_12 (
    .in0(in_1[11]), .in1(in_1[10]), .in2(in_1[9]), .in3(in_1[8]), .in4(in_1[7]), .in5(in_1[6]),
    .in6(in_1[5]), .in7(in_1[4]), .in8(in_1[3]), .in9(in_1[2]), .in10(in_1[1]), .in11(in_1[0]), .in12(1'b0),
    .in13(1'b0), .in14(1'b0), .in15(1'b0), .out(out_3[11]), .sel(SRL));  // open: en
  Multiplexer #(.select(4)) multiplexer_13 (
    .in0(in_1[12]), .in1(in_1[11]), .in2(in_1[10]), .in3(in_1[9]), .in4(in_1[8]), .in5(in_1[7]),
    .in6(in_1[6]), .in7(in_1[5]), .in8(in_1[4]), .in9(in_1[3]), .in10(in_1[2]), .in11(in_1[1]),
    .in12(in_1[0]), .in13(1'b0), .in14(1'b0), .in15(1'b0), .out(out_3[12]), .sel(SRL));  // open: en
  Multiplexer #(.select(4)) multiplexer_14 (
    .in0(in_1[13]), .in1(in_1[12]), .in2(in_1[11]), .in3(in_1[10]), .in4(in_1[9]), .in5(in_1[8]),
    .in6(in_1[7]), .in7(in_1[6]), .in8(in_1[5]), .in9(in_1[4]), .in10(in_1[3]), .in11(in_1[2]),
    .in12(in_1[1]), .in13(in_1[0]), .in14(1'b0), .in15(1'b0), .out(out_3[13]), .sel(SRL));  // open: en
  Multiplexer #(.select(4)) multiplexer_15 (
    .in0(in_1[14]), .in1(in_1[13]), .in2(in_1[12]), .in3(in_1[11]), .in4(in_1[10]), .in5(in_1[9]),
    .in6(in_1[8]), .in7(in_1[7]), .in8(in_1[6]), .in9(in_1[5]), .in10(in_1[4]), .in11(in_1[3]),
    .in12(in_1[2]), .in13(in_1[1]), .in14(in_1[0]), .in15(1'b0), .out(out_3[14]), .sel(SRL));  // open: en
  Multiplexer #(.select(4)) multiplexer_16 (
    .in0(in_1[15]), .in1(in_1[14]), .in2(in_1[13]), .in3(in_1[12]), .in4(in_1[11]), .in5(in_1[10]),
    .in6(in_1[9]), .in7(in_1[8]), .in8(in_1[7]), .in9(in_1[6]), .in10(in_1[5]), .in11(in_1[4]),
    .in12(in_1[3]), .in13(in_1[2]), .in14(in_1[1]), .in15(in_1[0]), .out(out_3[15]), .sel(SRL));  // open: en
endmodule

module _16bit_SRL (
  input  [15:0] in_1,
  input  [3:0] ShiftAmt,
  output [15:0] out_3
);

  Multiplexer #(.select(4)) multiplexer_1 (
    .in0(in_1[0]), .in1(in_1[1]), .in2(in_1[2]), .in3(in_1[3]), .in4(in_1[4]), .in5(in_1[5]), .in6(in_1[6]),
    .in7(in_1[7]), .in8(in_1[8]), .in9(in_1[9]), .in10(in_1[10]), .in11(in_1[11]), .in12(in_1[12]),
    .in13(in_1[13]), .in14(in_1[14]), .in15(in_1[15]), .out(out_3[0]), .sel(ShiftAmt));  // open: en
  Multiplexer #(.select(4)) multiplexer_2 (
    .in0(in_1[1]), .in1(in_1[2]), .in2(in_1[3]), .in3(in_1[4]), .in4(in_1[5]), .in5(in_1[6]), .in6(in_1[7]),
    .in7(in_1[8]), .in8(in_1[9]), .in9(in_1[10]), .in10(in_1[11]), .in11(in_1[12]), .in12(in_1[13]),
    .in13(in_1[14]), .in14(in_1[15]), .in15(1'b0), .out(out_3[1]), .sel(ShiftAmt));  // open: en
  Multiplexer #(.select(4)) multiplexer_3 (
    .in0(in_1[2]), .in1(in_1[3]), .in2(in_1[4]), .in3(in_1[5]), .in4(in_1[6]), .in5(in_1[7]), .in6(in_1[8]),
    .in7(in_1[9]), .in8(in_1[10]), .in9(in_1[11]), .in10(in_1[12]), .in11(in_1[13]), .in12(in_1[14]),
    .in13(in_1[15]), .in14(1'b0), .in15(1'b0), .out(out_3[2]), .sel(ShiftAmt));  // open: en
  Multiplexer #(.select(4)) multiplexer_4 (
    .in0(in_1[3]), .in1(in_1[4]), .in2(in_1[5]), .in3(in_1[6]), .in4(in_1[7]), .in5(in_1[8]), .in6(in_1[9]),
    .in7(in_1[10]), .in8(in_1[11]), .in9(in_1[12]), .in10(in_1[13]), .in11(in_1[14]), .in12(in_1[15]),
    .in13(1'b0), .in14(1'b0), .in15(1'b0), .out(out_3[3]), .sel(ShiftAmt));  // open: en
  Multiplexer #(.select(4)) multiplexer_5 (
    .in0(in_1[4]), .in1(in_1[5]), .in2(in_1[6]), .in3(in_1[7]), .in4(in_1[8]), .in5(in_1[9]), .in6(in_1[10]),
    .in7(in_1[11]), .in8(in_1[12]), .in9(in_1[13]), .in10(in_1[14]), .in11(in_1[15]), .in12(1'b0),
    .in13(1'b0), .in14(1'b0), .in15(1'b0), .out(out_3[4]), .sel(ShiftAmt));  // open: en
  Multiplexer #(.select(4)) multiplexer_6 (
    .in0(in_1[5]), .in1(in_1[6]), .in2(in_1[7]), .in3(in_1[8]), .in4(in_1[9]), .in5(in_1[10]),
    .in6(in_1[11]), .in7(in_1[12]), .in8(in_1[13]), .in9(in_1[14]), .in10(in_1[15]), .in11(1'b0),
    .in12(1'b0), .in13(1'b0), .in14(1'b0), .in15(1'b0), .out(out_3[5]), .sel(ShiftAmt));  // open: en
  Multiplexer #(.select(4)) multiplexer_7 (
    .in0(in_1[6]), .in1(in_1[7]), .in2(in_1[8]), .in3(in_1[9]), .in4(in_1[10]), .in5(in_1[11]),
    .in6(in_1[12]), .in7(in_1[13]), .in8(in_1[14]), .in9(in_1[15]), .in10(1'b0), .in11(1'b0), .in12(1'b0),
    .in13(1'b0), .in14(1'b0), .in15(1'b0), .out(out_3[6]), .sel(ShiftAmt));  // open: en
  Multiplexer #(.select(4)) multiplexer_8 (
    .in0(in_1[7]), .in1(in_1[8]), .in2(in_1[9]), .in3(in_1[10]), .in4(in_1[11]), .in5(in_1[12]),
    .in6(in_1[13]), .in7(in_1[14]), .in8(in_1[15]), .in9(1'b0), .in10(1'b0), .in11(1'b0), .in12(1'b0),
    .in13(1'b0), .in14(1'b0), .in15(1'b0), .out(out_3[7]), .sel(ShiftAmt));  // open: en
  Multiplexer #(.select(4)) multiplexer_9 (
    .in0(in_1[8]), .in1(in_1[9]), .in2(in_1[10]), .in3(in_1[11]), .in4(in_1[12]), .in5(in_1[13]),
    .in6(in_1[14]), .in7(in_1[15]), .in8(1'b0), .in9(1'b0), .in10(1'b0), .in11(1'b0), .in12(1'b0),
    .in13(1'b0), .in14(1'b0), .in15(1'b0), .out(out_3[8]), .sel(ShiftAmt));  // open: en
  Multiplexer #(.select(4)) multiplexer_10 (
    .in0(in_1[9]), .in1(in_1[10]), .in2(in_1[11]), .in3(in_1[12]), .in4(in_1[13]), .in5(in_1[14]),
    .in6(in_1[15]), .in7(1'b0), .in8(1'b0), .in9(1'b0), .in10(1'b0), .in11(1'b0), .in12(1'b0), .in13(1'b0),
    .in14(1'b0), .in15(1'b0), .out(out_3[9]), .sel(ShiftAmt));  // open: en
  Multiplexer #(.select(4)) multiplexer_11 (
    .in0(in_1[10]), .in1(in_1[11]), .in2(in_1[12]), .in3(in_1[13]), .in4(in_1[14]), .in5(in_1[15]),
    .in6(1'b0), .in7(1'b0), .in8(1'b0), .in9(1'b0), .in10(1'b0), .in11(1'b0), .in12(1'b0), .in13(1'b0),
    .in14(1'b0), .in15(1'b0), .out(out_3[10]), .sel(ShiftAmt));  // open: en
  Multiplexer #(.select(4)) multiplexer_12 (
    .in0(in_1[11]), .in1(in_1[12]), .in2(in_1[13]), .in3(in_1[14]), .in4(in_1[15]), .in5(1'b0), .in6(1'b0),
    .in7(1'b0), .in8(1'b0), .in9(1'b0), .in10(1'b0), .in11(1'b0), .in12(1'b0), .in13(1'b0), .in14(1'b0),
    .in15(1'b0), .out(out_3[11]), .sel(ShiftAmt));  // open: en
  Multiplexer #(.select(4)) multiplexer_13 (
    .in0(in_1[12]), .in1(in_1[13]), .in2(in_1[14]), .in3(in_1[15]), .in4(1'b0), .in5(1'b0), .in6(1'b0),
    .in7(1'b0), .in8(1'b0), .in9(1'b0), .in10(1'b0), .in11(1'b0), .in12(1'b0), .in13(1'b0), .in14(1'b0),
    .in15(1'b0), .out(out_3[12]), .sel(ShiftAmt));  // open: en
  Multiplexer #(.select(4)) multiplexer_14 (
    .in0(in_1[13]), .in1(in_1[14]), .in2(in_1[15]), .in3(1'b0), .in4(1'b0), .in5(1'b0), .in6(1'b0),
    .in7(1'b0), .in8(1'b0), .in9(1'b0), .in10(1'b0), .in11(1'b0), .in12(1'b0), .in13(1'b0), .in14(1'b0),
    .in15(1'b0), .out(out_3[13]), .sel(ShiftAmt));  // open: en
  Multiplexer #(.select(4)) multiplexer_15 (
    .in0(in_1[14]), .in1(in_1[15]), .in2(1'b0), .in3(1'b0), .in4(1'b0), .in5(1'b0), .in6(1'b0), .in7(1'b0),
    .in8(1'b0), .in9(1'b0), .in10(1'b0), .in11(1'b0), .in12(1'b0), .in13(1'b0), .in14(1'b0), .in15(1'b0),
    .out(out_3[14]), .sel(ShiftAmt));  // open: en
  Multiplexer #(.select(4)) multiplexer_16 (
    .in0(in_1[15]), .in1(1'b0), .in2(1'b0), .in3(1'b0), .in4(1'b0), .in5(1'b0), .in6(1'b0), .in7(1'b0),
    .in8(1'b0), .in9(1'b0), .in10(1'b0), .in11(1'b0), .in12(1'b0), .in13(1'b0), .in14(1'b0), .in15(1'b0),
    .out(out_3[15]), .sel(ShiftAmt));  // open: en
endmodule

module _16bit_sll_srl (
  input  [15:0] in_1,
  input  [3:0] in_2,
  input  in_3,
  output [15:0] out_4
);

  wire [15:0] n16bit_sll_1_out_3, n16bit_srl_1_out_3;

  _16bit_SLL u_16bit_sll_1 (.in_1(in_1), .SRL(in_2), .out_3(n16bit_sll_1_out_3));
  _16bit_SRL u_16bit_srl_1 (.in_1(in_1), .ShiftAmt(in_2), .out_3(n16bit_srl_1_out_3));
  Multiplexer #(.width(16)) multiplexer_1 (
    .in0(n16bit_sll_1_out_3), .in1(n16bit_srl_1_out_3), .out(out_4), .sel(in_3));  // open: en
endmodule

module _1_bit_ALU (
  input  B_prime,
  input  A,
  input  B,
  input  Cin,
  input  [2:0] in_5,
  output Result,
  output Cout
);

  wire adder_1_out, and_1_out, multiplexer_1_out, nor_1_out, not_1_out, or_1_out, xnor_1_out, xor_1_out;

  not not_1 (not_1_out, B);
  Multiplexer multiplexer_1 (.in0(B), .in1(not_1_out), .out(multiplexer_1_out), .sel(B_prime));  // open: en
  Adder #(.width(1)) adder_1 (.a(A), .b(multiplexer_1_out), .out(adder_1_out), .cin(Cin), .cout(Cout));
  and and_1 (and_1_out, A, B);
  or or_1 (or_1_out, A, B);
  nor nor_1 (nor_1_out, A, B);
  xor xor_1 (xor_1_out, A, B);
  xnor xnor_1 (xnor_1_out, A, B);
  Multiplexer #(.select(3)) multiplexer_2 (
    .in0(adder_1_out), .in1(and_1_out), .in2(or_1_out), .in3(nor_1_out), .in4(xor_1_out), .in5(xnor_1_out),
    .out(Result), .sel(in_5));  // open: in6, in7, en

  // Notes on the sheet:
  //   ALU op
endmodule

module _16_bit_ALU (
  input  [15:0] in_1,
  input  [15:0] B,
  input  Cin,
  input  B_prime,
  input  [2:0] OP,
  output F,
  output [15:0] out_7,
  output Cout
);

  wire n1_bit_alu_1_cout, n1_bit_alu_2_cout, n1_bit_alu_3_cout, n1_bit_alu_4_cout, n1_bit_alu_5_cout,
       n1_bit_alu_6_cout, n1_bit_alu_7_cout, n1_bit_alu_8_cout, n1_bit_alu_9_cout, n1_bit_alu_10_cout,
       n1_bit_alu_11_cout, n1_bit_alu_12_cout, n1_bit_alu_13_cout, n1_bit_alu_14_cout, n1_bit_alu_15_cout;

  _1_bit_ALU u_1_bit_alu_1 (
    .B_prime(B_prime), .A(B[0]), .B(in_1[0]), .Cin(Cin), .Result(out_7[0]), .Cout(n1_bit_alu_1_cout),
    .in_5(OP));
  _1_bit_ALU u_1_bit_alu_2 (
    .B_prime(B_prime), .A(B[1]), .B(in_1[1]), .Cin(n1_bit_alu_1_cout), .Result(out_7[1]),
    .Cout(n1_bit_alu_2_cout), .in_5(OP));
  _1_bit_ALU u_1_bit_alu_3 (
    .B_prime(B_prime), .A(B[2]), .B(in_1[2]), .Cin(n1_bit_alu_2_cout), .Result(out_7[2]),
    .Cout(n1_bit_alu_3_cout), .in_5(OP));
  _1_bit_ALU u_1_bit_alu_4 (
    .B_prime(B_prime), .A(B[3]), .B(in_1[3]), .Cin(n1_bit_alu_3_cout), .Result(out_7[3]),
    .Cout(n1_bit_alu_4_cout), .in_5(OP));
  _1_bit_ALU u_1_bit_alu_5 (
    .B_prime(B_prime), .A(B[4]), .B(in_1[4]), .Cin(n1_bit_alu_4_cout), .Result(out_7[4]),
    .Cout(n1_bit_alu_5_cout), .in_5(OP));
  _1_bit_ALU u_1_bit_alu_6 (
    .B_prime(B_prime), .A(B[5]), .B(in_1[5]), .Cin(n1_bit_alu_5_cout), .Result(out_7[5]),
    .Cout(n1_bit_alu_6_cout), .in_5(OP));
  _1_bit_ALU u_1_bit_alu_7 (
    .B_prime(B_prime), .A(B[6]), .B(in_1[6]), .Cin(n1_bit_alu_6_cout), .Result(out_7[6]),
    .Cout(n1_bit_alu_7_cout), .in_5(OP));
  _1_bit_ALU u_1_bit_alu_8 (
    .B_prime(B_prime), .A(B[7]), .B(in_1[7]), .Cin(n1_bit_alu_7_cout), .Result(out_7[7]),
    .Cout(n1_bit_alu_8_cout), .in_5(OP));
  _1_bit_ALU u_1_bit_alu_9 (
    .B_prime(B_prime), .A(B[8]), .B(in_1[8]), .Cin(n1_bit_alu_8_cout), .Result(out_7[8]),
    .Cout(n1_bit_alu_9_cout), .in_5(OP));
  _1_bit_ALU u_1_bit_alu_10 (
    .B_prime(B_prime), .A(B[9]), .B(in_1[9]), .Cin(n1_bit_alu_9_cout), .Result(out_7[9]),
    .Cout(n1_bit_alu_10_cout), .in_5(OP));
  _1_bit_ALU u_1_bit_alu_11 (
    .B_prime(B_prime), .A(B[10]), .B(in_1[10]), .Cin(n1_bit_alu_10_cout), .Result(out_7[10]),
    .Cout(n1_bit_alu_11_cout), .in_5(OP));
  _1_bit_ALU u_1_bit_alu_12 (
    .B_prime(B_prime), .A(B[11]), .B(in_1[11]), .Cin(n1_bit_alu_11_cout), .Result(out_7[11]),
    .Cout(n1_bit_alu_12_cout), .in_5(OP));
  _1_bit_ALU u_1_bit_alu_13 (
    .B_prime(B_prime), .A(B[12]), .B(in_1[12]), .Cin(n1_bit_alu_12_cout), .Result(out_7[12]),
    .Cout(n1_bit_alu_13_cout), .in_5(OP));
  _1_bit_ALU u_1_bit_alu_14 (
    .B_prime(B_prime), .A(B[13]), .B(in_1[13]), .Cin(n1_bit_alu_13_cout), .Result(out_7[13]),
    .Cout(n1_bit_alu_14_cout), .in_5(OP));
  _1_bit_ALU u_1_bit_alu_15 (
    .B_prime(B_prime), .A(B[14]), .B(in_1[14]), .Cin(n1_bit_alu_14_cout), .Result(out_7[14]),
    .Cout(n1_bit_alu_15_cout), .in_5(OP));
  _1_bit_ALU u_1_bit_alu_16 (
    .B_prime(B_prime), .A(B[15]), .B(in_1[15]), .Cin(n1_bit_alu_15_cout), .Result(out_7[15]), .Cout(Cout),
    .in_5(OP));
  nor nor_1 (F, out_7[0], out_7[1], out_7[2], out_7[3], out_7[4], out_7[5], out_7[6], out_7[7], out_7[8], out_7[9], out_7[10], out_7[11], out_7[12], out_7[13], out_7[14], out_7[15]);

  // Notes on the sheet:
  //   A
endmodule

module Write_Register (
  input  [3:0] Inout,
  output out_2
);

  wire and_1_out, and_2_out, not_1_out, not_2_out, not_3_out;

  not not_1 (not_1_out, Inout[2]);
  not not_2 (not_2_out, Inout[1]);
  not not_3 (not_3_out, Inout[0]);
  and and_1 (and_1_out, Inout[1], not_1_out);
  and and_2 (and_2_out, Inout[3], Inout[1], not_3_out);
  or or_1 (out_2, and_2_out, and_1_out, not_2_out);
endmodule

module ReqDst (
  input  [3:0] in_1,
  output out_2
);

  wire and_1_out, and_2_out, and_3_out, and_4_out, and_5_out, not_1_out, not_2_out, not_3_out, not_4_out,
       not_5_out, not_6_out;

  not not_1 (not_1_out, in_1[1]);
  not not_2 (not_2_out, in_1[1]);
  not not_3 (not_3_out, in_1[1]);
  not not_4 (not_4_out, in_1[2]);
  not not_5 (not_5_out, in_1[3]);
  not not_6 (not_6_out, in_1[0]);
  and and_1 (and_1_out, in_1[3], in_1[2], not_1_out);
  and and_2 (and_2_out, in_1[2], not_2_out, in_1[0]);
  and and_3 (and_3_out, in_1[3], not_3_out, in_1[0]);
  and and_4 (and_4_out, in_1[3], not_4_out, in_1[1]);
  and and_5 (and_5_out, not_5_out, in_1[2], in_1[1], not_6_out);
  or or_1 (out_2, and_1_out, and_2_out, and_3_out, and_4_out, and_5_out);
endmodule

module ALUsrc (
  input  [3:0] in_1,
  output out_2
);

  wire and_1_out, and_2_out, and_3_out, and_4_out, not_1_out, not_2_out, not_3_out, not_4_out;

  not not_1 (not_1_out, in_1[1]);
  not not_2 (not_2_out, in_1[2]);
  not not_3 (not_3_out, in_1[3]);
  not not_4 (not_4_out, in_1[0]);
  and and_1 (and_1_out, not_3_out, in_1[2], not_1_out, in_1[0]);
  and and_2 (and_2_out, not_3_out, in_1[2], in_1[1], not_4_out);
  and and_3 (and_3_out, in_1[3], not_2_out, in_1[0]);
  and and_4 (and_4_out, in_1[3], not_2_out, in_1[1]);
  or or_1 (out_2, and_1_out, and_2_out, and_3_out, and_4_out);
endmodule

module MemRead (
  input  [3:0] in_1,
  output out_2
);

  wire and_1_out, and_2_out, not_1_out, not_2_out, not_3_out;

  not not_1 (not_1_out, in_1[3]);
  not not_2 (not_2_out, in_1[1]);
  not not_3 (not_3_out, in_1[0]);
  and and_1 (and_1_out, not_1_out, in_1[2], not_2_out, in_1[0]);
  and and_2 (and_2_out, not_1_out, in_1[2], in_1[1], not_3_out);
  or or_1 (out_2, and_1_out, and_2_out);
endmodule

module ALUop (
  input  [3:0] in_1,
  output [2:0] out_2
);

  wire and_1_out, and_2_out, and_3_out, and_4_out, and_5_out, and_6_out, not_1_out, not_2_out, not_3_out,
       not_4_out, not_5_out, not_6_out, not_7_out, not_8_out, not_9_out, not_10_out, not_11_out, not_12_out,
       not_13_out, not_14_out, not_15_out;

  not not_1 (not_1_out, in_1[2]);
  not not_2 (not_2_out, in_1[3]);
  not not_3 (not_3_out, in_1[2]);
  and and_1 (and_1_out, not_2_out, not_3_out, in_1[1], in_1[0]);
  not not_4 (not_4_out, in_1[3]);
  and and_2 (and_2_out, not_4_out, in_1[2], not_5_out, not_6_out);
  not not_5 (not_5_out, in_1[1]);
  not not_6 (not_6_out, in_1[0]);
  and and_3 (and_3_out, in_1[3], not_1_out, in_1[1], in_1[0]);
  not not_7 (not_7_out, in_1[3]);
  not not_8 (not_8_out, in_1[2]);
  and and_4 (and_4_out, not_7_out, not_8_out, in_1[1], not_9_out);
  not not_9 (not_9_out, in_1[0]);
  not not_10 (not_10_out, in_1[3]);
  and and_5 (and_5_out, not_10_out, in_1[2], not_11_out, not_12_out);
  not not_11 (not_11_out, in_1[1]);
  not not_12 (not_12_out, in_1[0]);
  not not_13 (not_13_out, in_1[2]);
  and and_6 (and_6_out, in_1[3], not_13_out, in_1[1], not_14_out);
  not not_14 (not_14_out, in_1[0]);
  not not_15 (not_15_out, in_1[0]);
  and O2 (out_2[2], in_1[3], in_1[2], in_1[1], not_15_out);
  or O1 (out_2[1], and_1_out, and_2_out, and_3_out);
  or O0 (out_2[0], and_4_out, and_5_out, and_6_out);
endmodule

module Branch (
  input  [3:0] in_1,
  output out_2
);

  wire not_1_out;

  not not_1 (not_1_out, in_1[3]);
  and and_1 (out_2, not_1_out, in_1[2], in_1[1], in_1[0]);
endmodule

module jump (
  input  [3:0] in_1,
  output out_2
);

  and and_1 (out_2, in_1[3], in_1[2], in_1[1], in_1[0]);
endmodule

module Load (
  input  [3:0] in_1,
  output out_2
);

  and and_1 (out_2, in_1[3], in_1[2], in_1[1], in_1[0]);
endmodule

module Store (
  input  [3:0] in_1,
  output out_2
);

  wire not_1_out, not_2_out;

  not not_1 (not_1_out, in_1[3]);
  not not_2 (not_2_out, in_1[0]);
  and and_1 (out_2, not_1_out, in_1[2], in_1[1], not_2_out);
endmodule

module Binverse_Cin (
  input  [3:0] in_1,
  output out_2
);

  wire and_1_out, and_2_out, not_1_out, not_2_out, not_3_out;

  not not_1 (not_1_out, in_1[2]);
  not not_2 (not_2_out, in_1[1]);
  not not_3 (not_3_out, in_1[3]);
  and and_1 (and_1_out, not_3_out, not_1_out, not_2_out, in_1[0]);
  and and_2 (and_2_out, not_3_out, in_1[2], in_1[1], in_1[0]);
  or or_1 (out_2, and_1_out, and_2_out);
endmodule

module LR (
  input  [3:0] in_1,
  output out_2
);

  wire not_1_out;

  not not_1 (not_1_out, in_1[1]);
  and and_1 (out_2, in_1[3], in_1[2], not_1_out, in_1[0]);
endmodule

module Shift (
  input  [3:0] in_1,
  output out_2
);

  wire not_1_out;

  not not_1 (not_1_out, in_1[1]);
  and and_1 (out_2, in_1[3], in_1[2], not_1_out);
endmodule

module ControlUnit (
  input  [3:0] Opcode,
  output RegWrite,
  output Regdst,
  output AluSrc,
  output MemRead,
  output [2:0] ALUop,
  output Branch,
  output Jump,
  output Load,
  output Store,
  output B_prime_Cin,
  output L_R,
  output Shift
);

  ReqDst reqdst_1 (.in_1(Opcode), .out_2(Regdst));
  MemRead memread_1 (.in_1(Opcode), .out_2(AluSrc));
  MemRead memread_2 (.in_1(Opcode), .out_2(MemRead));
  ALUop aluop_1 (.in_1(Opcode), .out_2(ALUop));
  Branch branch_1 (.in_1(Opcode), .out_2(Branch));
  jump jump_1 (.in_1(Opcode), .out_2(Jump));
  Load load_1 (.in_1(Opcode), .out_2(Load));
  Store store_1 (.in_1(Opcode), .out_2(Store));
  Binverse_Cin binverse_cin_1 (.in_1(Opcode), .out_2(B_prime_Cin));
  LR lr_1 (.in_1(Opcode), .out_2(L_R));
  Shift shift_1 (.in_1(Opcode), .out_2(Shift));
  Write_Register write_register_1 (.Inout(Opcode), .out_2(RegWrite));
endmodule
